# Fritzing sketch Genius-Arduino (saved by Fritzing 0.9.2b)
circuit board: 8.46667cm x 5.64444cm
breadboards: 1

parts:
  Componente1 = Arduino Uno (Rev3)
  LED1 = smd LED [color="Red (633nm)" package="1206 [SMD]"]
  R1 = Resistor [tolerance=±5% resistance=330 package=THT]
  S1 = Pushbutton [package="[THT]"]
  R2 = Resistor [tolerance=±5% resistance=330 package=THT]
  R3 = Resistor [tolerance=±5% resistance=330 package=THT]
  R4 = Resistor [tolerance=±5% resistance=330 package=THT]
  LED2 = smd LED [color="Green (555nm)" package="0603 [SMD]"]
  LED3 = smd LED [color="Yellow (595nm)" package="0603 [SMD]"]
  LED4 = smd LED [color="Blue (430nm)" package="0603 [SMD]"]
  S2 = Pushbutton [package="[THT]"]
  S3 = Pushbutton [package="[THT]"]
  S4 = Pushbutton [package="[THT]"]

nets (from the breadboard view):
  N1: Componente1.D8, S2.Pin_1, S2.Pin_2
  N2: Componente1.D9_PWM, S3.Pin_1, S3.Pin_2
  N3: Componente1.D10_PWM/SS, S4.Pin_1, S4.Pin_2
  N4: Componente1.D11_PWM/MOSI, S1.Pin_1, S1.Pin_2
  N5: Componente1.D2, LED2.anode
  N6: Componente1.D3_PWM, LED3.anode
  N7: Componente1.D4, LED4.anode
  N8: Componente1.D5_PWM, LED1.anode
  N9: Componente1.GND, R1.Pin_0, S1.Pin_3, S1.Pin_4, R2.Pin_0, R3.Pin_0, R4.Pin_0, S2.Pin_3, S2.Pin_4, S3.Pin_3, S3.Pin_4, S4.Pin_3, S4.Pin_4
  N10: LED1.cathode, R1.Pin_1
  N11: R2.Pin_1, LED4.cathode
  N12: R3.Pin_1, LED3.cathode
  N13: R4.Pin_1, LED2.cathode
